# Fritzing sketch schema (saved by Fritzing 0.9.0b)
breadboards: 1

parts:
  Součástka1 = Arduino Pro Mini v13
  RHT1 = Humidity and Temperature Sensor RHT03
  T1 = DS18B20 Temperature Sensor [part_number=DS18B20 package="TO92 [THT]"]
  U1 = MAX485 [package=dil08]
  R1 = Resistor [tolerance=±5% resistance=120 package=THT]
  J1 = RJ9 [package=rj9]
  R2 = Resistor [tolerance=±5% resistance=4.7k package=THT]
  R3 = Resistor [tolerance=±5% resistance=4.7k package=THT]
  Součástka2 = Barometric Pressure Sensor - BMP085 Breakout

nets (from the breadboard view):
  VCC: Součástka1.VCC, RHT1.Vcc, T1.+Vdd, U1.RE, U1.DE, U1.VCC, R2.Pin_1, R3.Pin_1, Součástka2.VCC
  N1: Součástka1.A4, Součástka2.SDA
  N2: Součástka1.A5, Součástka2.SCL
  N3: Součástka1.RAW, J1.1
  GND: Součástka1.GND, RHT1.GND_2, T1.GND, U1.GND, R1.Pin_0, J1.4, Součástka2.GND
  N4: Součástka1.D10_PWM/SS, RHT1.Data-signal, R2.Pin_0
  N5: Součástka1.D8, T1.DQ, R3.Pin_0
  N6: Součástka1.D0/TX, U1.DI
  N7: U1.A, J1.2
  N8: U1.B, R1.Pin_1, J1.3

custom parts:
  DS18B20 Temperature Sensor: A DS18B20 temperature sensor
