# Fritzing sketch schema_pc (saved by Fritzing 0.9.0b)

parts:
  J1 = RJ9 [package=rj9]
  IC1 = Voltage Regulator [package=to-92]
  R1 = Resistor [tolerance=±5% resistance=120 package=THT]
  U1 = MAX485 [package=dil08]
  JP1 = FTDI_BASIC [package=ftdi_basic]
  R4 = Resistor [tolerance=±5% resistance=10k package=THT]
  R5 = Resistor [tolerance=±5% resistance=20k package=THT]
  R6 = Resistor [tolerance=±5% resistance=470 package=THT]
  R7 = Resistor [tolerance=±5% resistance=470 package=THT]

nets:
  9V: J1.1, IC1.IN
  N1: J1.2, R1.Pin_0, U1.A, R6.Pin_0
  N2: J1.3, R1.Pin_1, U1.B, R7.Pin_1
  GND: J1.4, IC1.GND, U1.RE, U1.DE, U1.GND, JP1.5, R5.Pin_0, R7.Pin_0
  5V: IC1.OUT, U1.VCC, R6.Pin_1
  N3: U1.RO, R4.Pin_1
  N4: JP1.1, R4.Pin_0, R5.Pin_1
